# Fritzing sketch Untitled Sketch (saved by Fritzing 0.9.3b)
breadboards: 3

parts:
  U1 = NodeMCU V1.0
  Part1 = Arduino Uno (Rev3) - ICSP
  7432 = CD4048B [part_number=CD4048B package="DIP (Dual Inline) [THT]"]
  IR1 = TSOP312.., 314.. [package=THT]
  LED1 = LED - 5mm [color="Red (633nm)" package="5 mm [THT]"]
  LED2 = LED - 5mm [color="Red (633nm)" package="5 mm [THT]"]
  LED3 = LED - 5mm [color="Red (633nm)" package="5 mm [THT]"]
  LED4 = LED - 5mm [color="Red (633nm)" package="5 mm [THT]"]
  RHT1 = Humidity and Temperature Sensor RHT03

nets:
  N1: U1.D1, 7432.A
  N2: U1.D2, 7432.C
  N3: U1.D3, 7432.J
  N4: U1.D4, 7432.F
  GND: U1.GND, Part1.GND, 7432.VSS, IR1.GND, RHT1.GND_1
  N5: U1.D8, RHT1.Vcc
  VIN: U1.Vin, Part1.5V, 7432.VDD, IR1.Vs, RHT1.GND_2
  N6: Part1.D8, 7432.EXPAND
  N7: Part1.D9_PWM, 7432.B
  N8: Part1.D10_PWM/SS, 7432.Kd
  N9: Part1.D11_PWM/MOSI, 7432.G
  N10: Part1.D2, IR1.Data
  N11: LED1.cathode, LED2.cathode, LED3.cathode, LED4.cathode

custom parts:
  NodeMCU V1.0: ESP8266 based NodeMCU
